# Fritzing sketch board (saved by Fritzing 0.9.4)
circuit board: 8.46667cm x 5.64444cm
breadboards: 1

parts:
  U1 = NodeMCU V3.0
  LED1 = LED - 5mm [color="Red (633nm)" package="5 mm [THT]"]
  LED2 = LED - 5mm [color="Yellow (595nm)" package="5 mm [THT]"]
  S1 = Pushbutton [package="[THT]"]
  LED3 = LED - 5mm [color="Green (565nm)" package="5 mm [THT]"]
  R4 = Resistor [tolerance=±5% resistance=10k package=THT]
  R2 = Resistor [tolerance=±5% resistance=100 package=THT]
  R1 = Resistor [tolerance=±5% resistance=100 package=THT]
  R3 = Resistor [tolerance=±5% resistance=100 package=THT]

nets:
  N1: U1.D1, R2.Pin_0
  N2: U1.D2, R1.Pin_0
  N3: U1.GND#6, U1.GND#13, U1.GND#16, U1.GND#33, LED1.anode, LED2.anode, LED3.anode, R4.Pin_1
  N4: U1.D5, R3.Pin_0
  N5: U1.D6, S1.Pin_1, S1.Pin_2, R4.Pin_0
  N6: U1.Vin, S1.Pin_3, S1.Pin_4
  N7: LED1.cathode, R2.Pin_1
  N8: LED2.cathode, R1.Pin_1
  N9: LED3.cathode, R3.Pin_1

custom parts:
  NodeMCU V3.0: ESP8266 based NodeMCU
